// Digital circuit main.dig as structural Verilog
module main (
  input  clock,
  input  pc_reset
);

  wire _32x32_1_p1, _32x32_1_p7, _32x32_1_p8, ex_mem_1_mem_memread, ex_mem_1_mem_memtoreg,
       ex_mem_1_mem_memwrite, ex_mem_1_wb_regwrite, id_ex_1_p16, id_ex_1_p17, id_ex_1_p18, id_ex_1_p19,
       id_ex_1_p20, id_ex_1_p21, id_ex_1_p22, instruction_mem_1_p2, mem_wb_1_wb_memtoreg, stall_1_stall,
       ula_1_p1;
  wire [1:0] FA, FB;
  wire [4:0] _32x32_1_p5, ex_mem_1_mem_dstaddr, multiplexer_2_out, undriven, undriven_2, undriven_3,
       undriven_5;
  wire [5:0] if_id_1_p4, if_id_1_p4_3;
  wire [7:0] control_1_mw, multiplexer_1_out;
  wire [25:6] if_id_1_p4_2;
  wire [31:0] add_1_s, bitextender_1_out, ex_mem_1_mem_result, ex_mem_1_mem_rtdata, id_ex_1_p23, id_ex_1_p24,
       mem_wb_1_wb_readdata, mem_wb_1_wb_result, memory_24x32_1_data, multiplexer_3_out, multiplexer_4_out,
       multiplexer_5_out, pc_1_p4, R31, ula_1_p5, undriven_4, WB;

  Seven_Seg_Hex seven_seg_hex_1 (.d(R31[19:16]), .dp(1'b0));
  Add #(.Bits(32)) add_1 (.a(pc_1_p4), .b(32'h4), .c_i(1'b0), .s(add_1_s));  // open: c_o
  // PC pc_1: pin names not known; wires that end beside it: clock, add_1_s, pc_reset, pc_1_p4
  Seven_Seg_Hex seven_seg_hex_2 (.d(R31[15:12]), .dp(1'b0));
  Seven_Seg_Hex seven_seg_hex_3 (.d(R31[11:8]), .dp(1'b0));
  // instruction_mem instruction_mem_1: pin names not known; wires that end beside it: pc_1_p4, instruction_mem_1_p2
  Seven_Seg_Hex seven_seg_hex_4 (.d(R31[7:4]), .dp(1'b0));
  Seven_Seg_Hex seven_seg_hex_5 (.d(R31[3:0]), .dp(1'b0));
  // IF_ID if_id_1: pin names not known; wires that end beside it: instruction_mem_1_p2, 1'b1, clock, {if_id_1_p4_3, if_id_1_p4_2, if_id_1_p4}
  Control control_1 (
    .RgD(control_1_mw[0]), .AluS(control_1_mw[1]), .MTR(control_1_mw[2]), .RW(control_1_mw[3]),
    .MR(control_1_mw[4]), .MW(control_1_mw[5]), .AO_1(control_1_mw[6]), .AO_0(control_1_mw[7]),
    .Op(if_id_1_p4_3), .Clk(clock));  // open: B, J, APC
  // _32x32 _32x32_1: pin names not known; wires that end beside it: _32x32_1_p1, WB, if_id_1_p4_2[25:21], if_id_1_p4_2[20:16], _32x32_1_p5, clock, _32x32_1_p7, _32x32_1_p8, R31
  BitExtender #(.inputBits(16), .outputBits(32)) bitextender_1 (
    .in({if_id_1_p4_2[15:6], if_id_1_p4}), .out(bitextender_1_out));
  Multiplexer #(.Bits(8)) multiplexer_1 (
    .sel(stall_1_stall), .in_0(control_1_mw), .in_1({8{1'b0}}), .out(multiplexer_1_out));
  Stall stall_1 (
    .IF_ID_rs(if_id_1_p4_2[25:21]), .IF_ID_rt(if_id_1_p4_2[20:16]), .ID_EX_memRead(id_ex_1_p18),
    .ID_EX_rt(undriven), .Stall(stall_1_stall));
  // ID_EX id_ex_1: pin names not known; wires that end beside it: multiplexer_1_out[3], multiplexer_1_out[2], multiplexer_1_out[4], multiplexer_1_out[5], multiplexer_1_out[0], multiplexer_1_out[1], multiplexer_1_out[7:6], _32x32_1_p7, _32x32_1_p8, bitextender_1_out, if_id_1_p4_2[25:21], if_id_1_p4_2[20:16], if_id_1_p4_2[15:11], if_id_1_p4, clock, id_ex_1_p16, id_ex_1_p17, id_ex_1_p18, id_ex_1_p19, id_ex_1_p20, id_ex_1_p21, id_ex_1_p22, id_ex_1_p23, id_ex_1_p24
  ALU_Control alu_control_1 (.AO_1(id_ex_1_p22), .F(undriven_3));  // open: AO_0, AC
  Multiplexer #(.Bits(5)) multiplexer_2 (
    .sel(id_ex_1_p20), .in_0(undriven), .in_1(undriven_2), .out(multiplexer_2_out));
  Multiplexer #(.Selector_Bits(2), .Bits(32)) multiplexer_3 (
    .sel(FB), .in_0(id_ex_1_p24), .in_1(WB), .in_2(ex_mem_1_mem_result), .in_3(ex_mem_1_mem_result),
    .out(multiplexer_3_out));
  Multiplexer #(.Selector_Bits(2), .Bits(32)) multiplexer_4 (
    .sel(FA), .in_0(id_ex_1_p23), .in_1(WB), .in_2(ex_mem_1_mem_result), .in_3(ex_mem_1_mem_result),
    .out(multiplexer_4_out));
  Multiplexer #(.Bits(32)) multiplexer_5 (
    .sel(id_ex_1_p21), .in_0(multiplexer_3_out), .in_1(undriven_4), .out(multiplexer_5_out));
  // ula ula_1: pin names not known; wires that end beside it: ula_1_p1, multiplexer_4_out, multiplexer_5_out, {6{1'b0}}, ula_1_p5
  forwarding_unit forwarding_unit_1 (
    .RS(undriven_5), .RT(undriven), .EX_MEM_dest(ex_mem_1_mem_dstaddr), .MEM_WB_dest(_32x32_1_p5),
    .EX_MEM_rw(ex_mem_1_wb_regwrite), .MEM_WB_rw(_32x32_1_p1), .FA(FA), .FB(FB));
  EX_MEM ex_mem_1 (
    .EX_regWrite(id_ex_1_p16), .EX_memRead(id_ex_1_p18), .EX_memWrite(id_ex_1_p19),
    .EX_memToReg(id_ex_1_p17), .EX_result(ula_1_p5), .EX_rtData(multiplexer_3_out),
    .EX_dstAddr(multiplexer_2_out), .clock(clock), .WB_regWrite(ex_mem_1_wb_regwrite),
    .MEM_memRead(ex_mem_1_mem_memread), .MEM_memWrite(ex_mem_1_mem_memwrite),
    .MEM_memToReg(ex_mem_1_mem_memtoreg), .MEM_result(ex_mem_1_mem_result), .MEM_rtData(ex_mem_1_mem_rtdata),
    .MEM_dstAddr(ex_mem_1_mem_dstaddr));
  memory_24x32 memory_24x32_1 (
    .address(ex_mem_1_mem_result[23:0]), .write_data(ex_mem_1_mem_rtdata), .mem_write(ex_mem_1_mem_memwrite),
    .mem_read(ex_mem_1_mem_memread), .clock(clock), .data(memory_24x32_1_data));
  MEM_WB mem_wb_1 (
    .MEM_regWrite(ex_mem_1_wb_regwrite), .MEM_memToReg(ex_mem_1_mem_memtoreg),
    .MEM_readData(memory_24x32_1_data), .MEM_result(ex_mem_1_mem_result), .MEM_dstAddr(ex_mem_1_mem_dstaddr),
    .clock(clock), .WB_regWrite(_32x32_1_p1), .WB_memToReg(mem_wb_1_wb_memtoreg),
    .WB_readData(mem_wb_1_wb_readdata), .WB_result(mem_wb_1_wb_result), .WB_dstAddr(_32x32_1_p5));
  Multiplexer #(.Bits(32)) multiplexer_6 (
    .sel(mem_wb_1_wb_memtoreg), .in_0(mem_wb_1_wb_result), .in_1(mem_wb_1_wb_readdata), .out(WB));

  // Notes on the sheet:
  //   Instruções na memória
  //   ADDI $S0, $S0, 5
  //   ADD $RA, $S0, $S0
  //   ADDI $RA, $RA, 5
  //   ADDI $RA, $RA, 5
  //   $S0 = 16, hex = 10
  //   $RA = 31, hex = 1F
  //   22100005
  //   0210f820
  //   23ff0005
  //   23ff0005
endmodule
